# Fritzing sketch Aedes (saved by Fritzing 0.9.3b)
breadboards: 1

parts:
  Multiplexer = Analog Digital MUX Breakout
  VCO_1_Octave = Rotary Potentiometer (Large) [maximum_resistance=10kΩ package=THT]
  Attack = Slide Potentiometer [maximum_resistance=100kΩ]
  Envelope_Switch = SWITCH_SPDT [package=kps-1290]
  Power_Switch = SPST Switch [package=switche-dpdt]
  D1 = Zener Diode [part_number=1N4732A breakdown_voltage=3.6V package="Melf DO-213 AB [SMD]"]
  R3 = Resistor [tolerance=±5% resistance=220 package=THT]
  RGB_LED = RGB LED (com. cathode, rbg) [package="5 mm [THT]"]
  Note_Button_1 = Square Pushbutton
  Bass_Boost_Button = Round Pushbutton
  Color_Cycling_RGB = LED - 5mm [color="Red (633nm)" package="5 mm [THT]"]
  Note_Button_2 = Square Pushbutton
  Note_Button_3 = Square Pushbutton
  Note_Button_4 = Square Pushbutton
  Note_Button_5 = Square Pushbutton
  Note_Button_6 = Square Pushbutton
  Note_Button_7 = Square Pushbutton
  Note_Button_8 = Square Pushbutton
  Modge_Toggle_Button = Square Pushbutton
  Decay = Slide Potentiometer [maximum_resistance=100kΩ]
  Sustain = Slide Potentiometer [maximum_resistance=100kΩ]
  Release = Slide Potentiometer [maximum_resistance=100kΩ]
  Volume = Slide Potentiometer [maximum_resistance=100kΩ]
  VCO_1_Shape = Rotary Potentiometer (Large) [maximum_resistance=10kΩ package=THT]
  VCO_1_&_VCO_2_Mix = Rotary Potentiometer (Large) [maximum_resistance=10kΩ package=THT]
  VCO_2_Octave = Rotary Potentiometer (Large) [maximum_resistance=10kΩ package=THT]
  VCO_2_Shape = Rotary Potentiometer (Large) [maximum_resistance=10kΩ package=THT]
  VCO_2_Detune = Rotary Potentiometer (Large) [maximum_resistance=10kΩ package=THT]
  VCO_Width/Mod = Rotary Potentiometer (Large) [maximum_resistance=10kΩ package=THT]
  LFO_Frequency = Rotary Potentiometer (Large) [maximum_resistance=10kΩ package=THT]
  LFO_Shape = Rotary Potentiometer (Large) [maximum_resistance=10kΩ package=THT]
  LFO_Noise = Rotary Potentiometer (Large) [maximum_resistance=10kΩ package=THT]
  Filter_Resonance = Rotary Potentiometer (Large) [maximum_resistance=10kΩ package=THT]
  Filter_Mix = Rotary Potentiometer (Large) [maximum_resistance=10kΩ package=THT]
  Filter_Cutoff = Rotary Potentiometer (Large) [maximum_resistance=10kΩ package=THT]
  Filter_LFO_Mix = Rotary Potentiometer (Large) [maximum_resistance=10kΩ package=THT]
  Delay_Feedback = Rotary Potentiometer (Large) [maximum_resistance=10kΩ package=THT]
  Delay_Time = Rotary Potentiometer (Large) [maximum_resistance=10kΩ package=THT]
  Key = Rotary Potentiometer (Large) [maximum_resistance=10kΩ package=THT]
  Teensy_3_2 = Teensy 3.0
  R28 = Resistor [tolerance=±5% resistance=220 package=THT]
  R29 = Resistor [tolerance=±5% resistance=220 package=THT]
  R30 = Resistor [tolerance=±5% resistance=220 package=THT]
  Power_Connector = Power Jack [package=power_jack_pth]

nets:
  N1: Multiplexer.C0, VCO_1_Octave.wiper
  N2: Multiplexer.C1, VCO_1_Shape.wiper
  N3: Multiplexer.C2, VCO_1_&_VCO_2_Mix.wiper
  N4: Multiplexer.C3, VCO_2_Octave.wiper
  N5: Multiplexer.C4, VCO_2_Shape.wiper
  N6: Multiplexer.C5, VCO_2_Detune.wiper
  N7: Multiplexer.C6, VCO_Width/Mod.wiper
  N8: Multiplexer.C7, LFO_Frequency.wiper
  N9: Multiplexer.C8, LFO_Shape.wiper
  N10: Multiplexer.C9, LFO_Noise.wiper
  N11: Multiplexer.C10, Delay_Time.wiper
  N12: Multiplexer.C11, Delay_Feedback.wiper
  N13: Multiplexer.C12, Filter_Cutoff.wiper
  N14: Multiplexer.C13, Filter_Resonance.wiper
  N15: Multiplexer.C14, Filter_LFO_Mix.wiper
  N16: Multiplexer.C15, Filter_Mix.wiper
  GND: Multiplexer.GND, VCO_1_Octave.leg2, Attack.leg2, Envelope_Switch.P, Power_Switch.S, RGB_LED.common_cathode, Note_Button_1.leg1, Bass_Boost_Button.leg1, Note_Button_2.leg1, Note_Button_3.leg1, Note_Button_4.leg1, Note_Button_5.leg1, Note_Button_6.leg1, Note_Button_7.leg1, Note_Button_8.leg1, Modge_Toggle_Button.leg1, Decay.leg2, Sustain.leg2, Release.leg2, Volume.leg2, VCO_1_Shape.leg2, VCO_1_&_VCO_2_Mix.leg2, VCO_2_Octave.leg2, VCO_2_Shape.leg2, VCO_2_Detune.leg2, VCO_Width/Mod.leg2, LFO_Frequency.leg2, LFO_Shape.leg2, LFO_Noise.leg2, Filter_Resonance.leg2, Filter_Mix.leg2, Filter_Cutoff.leg2, Filter_LFO_Mix.leg2, Delay_Feedback.leg2, Delay_Time.leg2, Key.leg2, Teensy_3_2.GND
  VCC: Multiplexer.VCC, VCO_1_Octave.leg1, Attack.leg1, Decay.leg1, Sustain.leg1, Release.leg1, Volume.leg1, VCO_1_Shape.leg1, VCO_1_&_VCO_2_Mix.leg1, VCO_2_Octave.leg1, VCO_2_Shape.leg1, VCO_2_Detune.leg1, VCO_Width/Mod.leg1, LFO_Frequency.leg1, LFO_Shape.leg1, LFO_Noise.leg1, Filter_Resonance.leg1, Filter_Mix.leg1, Filter_Cutoff.leg1, Filter_LFO_Mix.leg1, Delay_Feedback.leg1, Delay_Time.leg1, Key.wiper, Teensy_3_2.3V3
  N17: Multiplexer.S0, Teensy_3_2.D27
  N18: Multiplexer.S1, Teensy_3_2.D26
  N19: Multiplexer.S2, Teensy_3_2.D25
  N20: Multiplexer.S3, Teensy_3_2.D24
  N21: Multiplexer.SIG, Teensy_3_2.D28
  N22: Attack.wiper, Teensy_3_2.D29
  N23: Envelope_Switch.O, Teensy_3_2.D32
  N24: Power_Switch.P, Power_Connector.GNDBREAK
  N25: D1.cathode, Teensy_3_2.Vin, R30.Pin_0
  N26: D1.anode, Power_Connector.PWR
  N27: R3.Pin_0, RGB_LED.red_anode
  N28: R3.Pin_1, Teensy_3_2.D3
  N29: RGB_LED.blue_anode, R28.Pin_0
  N30: RGB_LED.green_anode, R29.Pin_0
  N31: Note_Button_1.leg0, Teensy_3_2.D0
  N32: Bass_Boost_Button.leg0, Color_Cycling_RGB.cathode, Teensy_3_2.D33
  N33: Color_Cycling_RGB.anode, R30.Pin_1
  N34: Note_Button_2.leg0, Teensy_3_2.D1
  N35: Note_Button_3.leg0, Teensy_3_2.D2
  N36: Note_Button_4.leg0, Teensy_3_2.D6
  N37: Note_Button_5.leg0, Teensy_3_2.A2/D16
  N38: Note_Button_6.leg0, Teensy_3_2.A3/D17
  N39: Note_Button_7.leg0, Teensy_3_2.A6/D20
  N40: Note_Button_8.leg0, Teensy_3_2.A7/D21
  N41: Modge_Toggle_Button.leg0, Teensy_3_2.A10
  N42: Decay.wiper, Teensy_3_2.D30
  N43: Sustain.wiper, Teensy_3_2.D31
  N44: Release.wiper, Teensy_3_2.A12
  N45: Volume.wiper, Teensy_3_2.A1/D15
  N46: Key.leg1, Teensy_3_2.A13
  N47: Teensy_3_2.D4, R28.Pin_1
  N48: Teensy_3_2.D5, R29.Pin_1
