# Fritzing sketch v3.1 (saved by Fritzing 0.9.3b)
breadboards: 1

parts:
  Multiplexer = Analog Digital MUX Breakout
  VCO_1_Octave = Rotary Potentiometer (Large) [maximum_resistance=10kΩ package=THT]
  Attack = Slide Potentiometer [maximum_resistance=100kΩ]
  Envelope_Switch = SWITCH_SPDT [package=kps-1290]
  Power_Switch = SPST Switch [package=switche-dpdt]
  R3 = Resistor [tolerance=±5% resistance=220 package=THT]
  RGB_LED = RGB LED (com. cathode, rbg) [package="5 mm [THT]"]
  Bass_Boost_Button = Round Pushbutton
  Color_Cycling_RGB = LED - 5mm [color="Red (633nm)" package="5 mm [THT]"]
  Note_C = Square Pushbutton
  Note_C# = Square Pushbutton
  Note_D = Square Pushbutton
  Note_D# = Square Pushbutton
  Note_E = Square Pushbutton
  Note_F# = Square Pushbutton
  Note_G = Square Pushbutton
  Decay = Slide Potentiometer [maximum_resistance=100kΩ]
  Sustain = Slide Potentiometer [maximum_resistance=100kΩ]
  Release = Slide Potentiometer [maximum_resistance=100kΩ]
  VCO_1_Shape = Rotary Potentiometer (Large) [maximum_resistance=10kΩ package=THT]
  VCO_1_&_VCO_2_Mix = Rotary Potentiometer (Large) [maximum_resistance=10kΩ package=THT]
  VCO_2_Octave = Rotary Potentiometer (Large) [maximum_resistance=10kΩ package=THT]
  VCO_2_Shape = Rotary Potentiometer (Large) [maximum_resistance=10kΩ package=THT]
  VCO_2_Detune = Rotary Potentiometer (Large) [maximum_resistance=10kΩ package=THT]
  VCO_Width/Mod = Rotary Potentiometer (Large) [maximum_resistance=10kΩ package=THT]
  LFO_Frequency = Rotary Potentiometer (Large) [maximum_resistance=10kΩ package=THT]
  LFO_Shape = Rotary Potentiometer (Large) [maximum_resistance=10kΩ package=THT]
  LFO_Noise = Rotary Potentiometer (Large) [maximum_resistance=10kΩ package=THT]
  Filter_Resonance = Rotary Potentiometer (Large) [maximum_resistance=10kΩ package=THT]
  Filter_Mix = Rotary Potentiometer (Large) [maximum_resistance=10kΩ package=THT]
  Filter_Cutoff = Rotary Potentiometer (Large) [maximum_resistance=10kΩ package=THT]
  Filter_LFO_Mix = Rotary Potentiometer (Large) [maximum_resistance=10kΩ package=THT]
  Delay_Feedback = Rotary Potentiometer (Large) [maximum_resistance=10kΩ package=THT]
  Delay_Time = Rotary Potentiometer (Large) [maximum_resistance=10kΩ package=THT]
  Key = Rotary Potentiometer (Large) [maximum_resistance=10kΩ package=THT]
  R28 = Resistor [tolerance=±5% resistance=220 package=THT]
  R29 = Resistor [tolerance=±5% resistance=220 package=THT]
  R30 = Resistor [tolerance=±5% resistance=220 package=THT]
  Teensy_3_6 = IC, DIP package, 72 pins [chip_label="Teensy 3.6"]
  Note_F = Square Pushbutton
  Note_A = Square Pushbutton
  Note_G# = Square Pushbutton
  Note_B = Square Pushbutton
  Note_A# = Square Pushbutton
  Note_C2 = Square Pushbutton
  Power = DC Power [voltage=5V]
  Teensy_3_2 = Teensy 3.0
  Audio_Board_1 = IC, DIP package, 46 pins [chip_label=Audio]
  Audio_Board_2 = Teensy Audio Board [package="DIP (Dual Inline) [THT]"]
  Color_Cycling_RGB1 = LED - 5mm [color="Red (633nm)" package="5 mm [THT]"]
  R31 = Resistor [tolerance=±5% resistance=220 package=THT]
  Button_Matrix = Trellis Monochrome Driver PCB for 4x4 Keypad and 3mm LEDs [part_number=1616]
  Preset_1 = Square Pushbutton
  Preset_2 = Square Pushbutton
  Preset_3 = Square Pushbutton
  Preset_4 = Square Pushbutton
  Preset_5 = Square Pushbutton
  Preset_6 = Square Pushbutton
  Bitcrusher_Freq = Slide Potentiometer [maximum_resistance=100kΩ]
  Bitcrusher_Bit_Rate = Slide Potentiometer [maximum_resistance=100kΩ]
  Volume_Master = Slide Potentiometer [maximum_resistance=100kΩ]
  Volume_SparkPunk = Slide Potentiometer [maximum_resistance=100kΩ]
  Volume_Nebulophone = Slide Potentiometer [maximum_resistance=100kΩ]
  Volume_PolySynth = Slide Potentiometer [maximum_resistance=100kΩ]
  Volume_Drums = Slide Potentiometer [maximum_resistance=100kΩ]
  Volume_Line-In = Slide Potentiometer [maximum_resistance=100kΩ]
  Amplifier = Adafruit Stereo 2.8W Class D Audio Amplifier - I2C Control AGC - TPA2016 [part_number="Adafruit #1712"]
  SPKR1 = Loudspeaker
  SPKR2 = Loudspeaker
  Split_Voice_Switch = SWITCH_SPDT [package=kps-1290]
  SparkPunk = SIP - 2 pins [chip_label=IC package="SIP (Single Inline) [THT]"]
  Nebulophone = SIP - 2 pins [chip_label=IC package="SIP (Single Inline) [THT]"]
  Raspberry_Pi = SIP - 2 pins [chip_label=IC package="SIP (Single Inline) [THT]"]
  Line_In = Audio Jack (TRS) 3.5mm [package="PG203J [THT]"]
  Drum_Mode_Switch = NKK M2032SS1W01 3PDT Toggle Switch [part_number="3 way switch" package=THT]
  R32 = Resistor [tolerance=±5% resistance=220 package=THT]
  R33 = Resistor [tolerance=±5% resistance=2.2k package=THT]
  R34 = Resistor [tolerance=±5% resistance=10k package=THT]
  Sync_3 = Square Pushbutton
  Sync_2 = Square Pushbutton
  Sync_1 = Square Pushbutton
  Sync_4 = Square Pushbutton
  OctoWS2811 = IC, SIP package, 13 pins

nets:
  N1: Multiplexer.C0, VCO_1_Octave.wiper
  N2: Multiplexer.C1, VCO_1_Shape.wiper
  N3: Multiplexer.C2, VCO_1_&_VCO_2_Mix.wiper
  N4: Multiplexer.C3, VCO_2_Octave.wiper
  N5: Multiplexer.C4, VCO_2_Shape.wiper
  N6: Multiplexer.C5, VCO_2_Detune.wiper
  N7: Multiplexer.C6, VCO_Width/Mod.wiper
  N8: Multiplexer.C7, LFO_Frequency.wiper
  N9: Multiplexer.C8, LFO_Shape.wiper
  N10: Multiplexer.C9, LFO_Noise.wiper
  N11: Multiplexer.C10, Delay_Time.wiper
  N12: Multiplexer.C11, Delay_Feedback.wiper
  N13: Multiplexer.C12, Filter_Cutoff.wiper
  N14: Multiplexer.C13, Filter_Resonance.wiper
  N15: Multiplexer.C14, Filter_LFO_Mix.wiper
  N16: Multiplexer.C15, Filter_Mix.wiper
  N17: Multiplexer.GND, VCO_1_Octave.leg2, Attack.leg2, Envelope_Switch.P, Power_Switch.S, RGB_LED.common_cathode, Bass_Boost_Button.leg1, Note_C.leg1, Note_C#.leg1, Note_D.leg1, Note_D#.leg1, Note_E.leg1, Note_F#.leg1, Note_G.leg1, Decay.leg2, Sustain.leg2, Release.leg2, VCO_1_Shape.leg2, VCO_1_&_VCO_2_Mix.leg2, VCO_2_Octave.leg2, VCO_2_Shape.leg2, VCO_2_Detune.leg2, VCO_Width/Mod.leg2, LFO_Frequency.leg2, LFO_Shape.leg2, LFO_Noise.leg2, Filter_Resonance.leg2, Filter_Mix.leg2, Filter_Cutoff.leg2, Filter_LFO_Mix.leg2, Delay_Feedback.leg2, Delay_Time.leg2, Key.leg2, Note_F.leg1, Note_A.leg1, Note_G#.leg1, Note_B.leg1, Note_A#.leg1, Note_C2.leg1, Color_Cycling_RGB1.cathode, Preset_1.leg1, Preset_2.leg1, Preset_3.leg1, Preset_4.leg1, Preset_5.leg1, Preset_6.leg1, Bitcrusher_Freq.leg2, Bitcrusher_Bit_Rate.leg2, Volume_Master.leg2, Volume_SparkPunk.leg2, Volume_Nebulophone.leg2, Volume_PolySynth.leg2, Volume_Drums.leg2, Volume_Line-In.leg2, Split_Voice_Switch.P
  N18: Multiplexer.VCC, VCO_1_Octave.leg1, Attack.leg1, Decay.leg1, Sustain.leg1, Release.leg1, VCO_1_Shape.leg1, VCO_1_&_VCO_2_Mix.leg1, VCO_2_Octave.leg1, VCO_2_Shape.leg1, VCO_2_Detune.leg1, VCO_Width/Mod.leg1, LFO_Frequency.leg1, LFO_Shape.leg1, LFO_Noise.leg1
  N19: Multiplexer.S0, Teensy_3_6.pin19
  N20: Multiplexer.S1, Teensy_3_6.pin18
  N21: Multiplexer.S2, Teensy_3_6.pin17
  N22: Multiplexer.S3, Teensy_3_6.pin16
  N23: Multiplexer.SIG, Teensy_3_6.pin20
  N24: Attack.wiper, Teensy_3_6.pin62
  N25: Envelope_Switch.O, Teensy_3_6.pin32
  N26: Power_Switch.P, Power.V+
  N27: R3.Pin_0, RGB_LED.red_anode
  N28: R3.Pin_1, Teensy_3_6.pin4
  N29: RGB_LED.blue_anode, R28.Pin_0
  N30: RGB_LED.green_anode, R29.Pin_0
  N31: Bass_Boost_Button.leg0, Color_Cycling_RGB.cathode
  N32: Color_Cycling_RGB.anode, R30.Pin_1
  N33: Note_C.leg0, Teensy_3_6.pin7
  N34: Note_C#.leg0, Teensy_3_6.pin10
  N35: Note_D.leg0, Teensy_3_6.pin30
  N36: Note_D#.leg0, Teensy_3_6.pin29
  N37: Note_E.leg0, Teensy_3_6.pin28
  N38: Note_F#.leg0, Teensy_3_6.pin26
  N39: Note_G.leg0, Teensy_3_6.pin47
  N40: Decay.wiper, Teensy_3_6.pin63
  N41: Sustain.wiper, Teensy_3_6.pin66
  N42: Release.wiper, Teensy_3_6.pin67
  N43: Filter_Resonance.leg1, Filter_Mix.leg1, Filter_Cutoff.leg1, Filter_LFO_Mix.leg1, Delay_Feedback.leg1, Delay_Time.leg1, Key.leg1, Bitcrusher_Freq.leg1, Bitcrusher_Bit_Rate.leg1
  N44: Key.wiper, Teensy_3_6.pin35
  N45: R28.Pin_1, Teensy_3_6.pin5
  N46: R29.Pin_1, Teensy_3_6.pin6
  VIN: R30.Pin_0, Teensy_3_6.pin72, Power.V-, Teensy_3_2.Vin, Audio_Board_1.pin46, Button_Matrix.VCC, Volume_Master.leg1, Volume_SparkPunk.leg1, Volume_Nebulophone.leg1, Volume_PolySynth.leg1, Volume_Drums.leg1, Volume_Line-In.leg1, OctoWS2811.pin13
  N47: Teensy_3_6.pin1, Audio_Board_1.pin1
  N48: Teensy_3_6.pin2, Teensy_3_2.D3
  N49: Teensy_3_6.pin3, Teensy_3_2.D4
  N50: Teensy_3_6.pin8, Audio_Board_1.pin8
  N51: Teensy_3_6.pin9, Audio_Board_1.pin9, Audio_Board_2.7
  N52: Teensy_3_6.pin11, Audio_Board_1.pin11, Audio_Board_2.9
  N53: Teensy_3_6.pin12, Audio_Board_1.pin12, Audio_Board_2.10
  N54: Teensy_3_6.pin13, Audio_Board_1.pin13, Audio_Board_2.11
  N55: Teensy_3_6.pin14, Audio_Board_1.pin14, Audio_Board_2.12
  N56: Teensy_3_6.pin22, Split_Voice_Switch.O
  N57: Teensy_3_6.pin23, Volume_Nebulophone.wiper
  N58: Teensy_3_6.pin24, Volume_PolySynth.wiper
  N59: Teensy_3_6.pin27, Note_F.leg0
  N60: Teensy_3_6.pin31, Button_Matrix.INT
  N61: Teensy_3_6.pin36, Volume_SparkPunk.wiper
  N62: Teensy_3_6.pin37, Preset_2.leg0
  N63: Teensy_3_6.pin38, Preset_1.leg0
  N64: Teensy_3_6.pin40, Note_C2.leg0
  N65: Teensy_3_6.pin41, Note_B.leg0
  N66: Teensy_3_6.pin42, Note_A#.leg0
  N67: Teensy_3_6.pin43, Note_A.leg0
  N68: Teensy_3_6.pin44, Preset_6.leg0
  N69: Teensy_3_6.pin45, Preset_5.leg0
  N70: Teensy_3_6.pin46, Note_G#.leg0
  N71: Teensy_3_6.pin49, Volume_Drums.wiper
  N72: Teensy_3_6.pin50, Volume_Line-In.wiper
  N73: Teensy_3_6.pin51, Volume_Master.wiper
  N74: Teensy_3_6.pin52, Bitcrusher_Freq.wiper
  N75: Teensy_3_6.pin53, Bitcrusher_Bit_Rate.wiper
  N76: Teensy_3_6.pin54, Audio_Board_2.13
  N77: Teensy_3_6.pin55, Drum_Mode_Switch.C1, Drum_Mode_Switch.C2, Drum_Mode_Switch.C3
  N78: Teensy_3_6.pin56, Preset_3.leg0
  N79: Teensy_3_6.pin57, Preset_4.leg0
  N80: Teensy_3_6.pin59, Audio_Board_1.pin33
  N81: Teensy_3_6.pin60, Audio_Board_1.pin34, Audio_Board_2.14
  N82: Teensy_3_6.pin61, Audio_Board_1.pin35, Audio_Board_2.15, Audio_Board_2.22
  N83: Teensy_3_6.pin64, Audio_Board_1.pin38, Audio_Board_2.18
  N84: Teensy_3_6.pin65, Audio_Board_1.pin39, Audio_Board_2.19, Button_Matrix.SCL
  N85: Teensy_3_6.pin68, Audio_Board_1.pin42, Button_Matrix.SDA
  N86: Teensy_3_6.pin69, Audio_Board_1.pin43, Audio_Board_2.23
  N87: Teensy_3_6.pin70, Audio_Board_1.pin44, Audio_Board_2.3V
  N88: Teensy_3_6.pin71, Teensy_3_2.GND, Audio_Board_1.pin45, R32.Pin_1, R33.Pin_1, R34.Pin_1, Sync_3.leg1, Sync_2.leg1, Sync_1.leg1, Sync_4.leg1, OctoWS2811.pin12
  N89: Teensy_3_2.D0, OctoWS2811.pin1
  N90: Teensy_3_2.D5, OctoWS2811.pin8
  N91: Teensy_3_2.D6, OctoWS2811.pin5
  N92: Teensy_3_2.D7, OctoWS2811.pin3
  N93: Teensy_3_2.D8, OctoWS2811.pin4
  N94: Teensy_3_2.D12, OctoWS2811.pin11
  N95: Teensy_3_2.A0/D14, OctoWS2811.pin2
  N96: Teensy_3_2.A1/D15, OctoWS2811.pin9
  N97: Teensy_3_2.A2/D16, OctoWS2811.pin10
  N98: Teensy_3_2.A6/D20, OctoWS2811.pin6
  N99: Teensy_3_2.A7/D21, OctoWS2811.pin7
  N100: Teensy_3_2.A11, Sync_4.leg0
  N101: Teensy_3_2.A10, Sync_3.leg0
  N102: Teensy_3_2.D25, Teensy_3_2.D32
  N103: Teensy_3_2.A12, Sync_2.leg0
  N104: Teensy_3_2.A13, Sync_1.leg0
  N105: Audio_Board_1.pin24, Nebulophone.pin2
  N106: Audio_Board_1.pin25, Nebulophone.pin1
  N107: Audio_Board_1.pin26, SparkPunk.pin2
  N108: Audio_Board_1.pin27, SparkPunk.pin1
  GND: Audio_Board_2.GND, Button_Matrix.GND
  N109: Audio_Board_2.LIn-L, Line_In.Ring
  N110: Audio_Board_2.LIn-GNDL, Line_In.Sleeve, Line_In.Tip
  N111: Audio_Board_2.LIn-R, Raspberry_Pi.pin2
  N112: Audio_Board_2.LIn-GNDR, Raspberry_Pi.pin1
  N113: Audio_Board_2.LOut-R1, Amplifier.IN_R_P
  N114: Audio_Board_2.LOut-GND, Amplifier.IN_R_N, Amplifier.IN_L_N
  N115: Audio_Board_2.LOut-L1, Amplifier.IN_L_P
  N116: Color_Cycling_RGB1.anode, R31.Pin_1
  N117: Amplifier.OUT_L_N, SPKR2.pin2
  N118: Amplifier.OUT_L_P, SPKR2.pin1
  N119: Amplifier.OUT_R_P, SPKR1.pin1
  N120: Amplifier.OUT_R_N, SPKR1.pin2
  N121: Drum_Mode_Switch.L1-1, R32.Pin_0
  N122: Drum_Mode_Switch.L2-2, R33.Pin_0
  N123: Drum_Mode_Switch.L3-2, R34.Pin_0

custom parts:
  Trellis Monochrome Driver PCB for 4x4 Keypad and 3mm LEDs: Trellis is an open source backlight keypad driver system. It is easy to use, works with any 3mm LEDs and eight tiles can be tiled together on a shared I2C bus. This PCB is specially made to match the Adafruit 4x4 elastomer keypad. Each Trellis PCB has 4x4 pads and 4x4 matching spots for 3mm LEDs. The circuitry on-board handles the background key-presses and LED lighting for the 4x4 tile.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
  Adafruit Stereo 2.8W Class D Audio Amplifier - I2C Control AGC - TPA2016: A mini class D with AGC and I2C control? Yes please! This incredibly small stereo amplifier is surprisingly powerful. It is able to deliver 2 x 2.8W channels into 4 ohm impedance speakers (@ 10% THD) and it has a i2c control interface as well as an AGC (automatic gain control) system to keep your audio from clipping or distorting. If you don't want to use I2C to control it, it does start up on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
  NKK M2032SS1W01 3PDT Toggle Switch: NKK M2032SS1W01 3PDT Toggle Switch This switch has three poles and two position
